// Logisim project 1lab.circ as structural Verilog: 16 circuits, main circuit o_not
module main (
  input  in_1,
  input  in_2,
  input  in_3,
  input  in_4,
  input  in_5,
  input  in_6,
  input  in_7,
  input  in_8,
  output out_9,
  output out_10,
  output out_11,
  output out_12,
  output out_13
);

  // NAND_Gate nand_1 has open pins: out=out_9
  o_not o_not_1 (.a(in_2), .out_2(out_10));
  o_and o_and_1 (.a(in_3), .b(in_4), .out_3(out_11));
  o_or o_or_1 (.b(in_6), .a(in_5), .out_3(out_12));
  o_xor o_xor_1 (.a(in_7), .b(in_8), .out_3(out_13));
endmodule

module o_not (
  input  a,
  output out_2
);

  nand nand_1 (out_2, a, a);
endmodule

module o_and (
  input  a,
  input  b,
  output out_3
);

  wire nand_1_out;

  nand nand_1 (nand_1_out, a, b);
  o_not o_not_1 (.a(nand_1_out), .out_2(out_3));
endmodule

module o_or (
  input  a,
  input  b,
  output out_3
);

  wire o_and_1_out_3, o_not_1_out_2, o_not_2_out_2;

  o_not o_not_1 (.a(a), .out_2(o_not_1_out_2));
  o_not o_not_2 (.a(b), .out_2(o_not_2_out_2));
  o_and o_and_1 (.a(o_not_1_out_2), .b(o_not_2_out_2), .out_3(o_and_1_out_3));
  o_not o_not_3 (.a(o_and_1_out_3), .out_2(out_3));
endmodule

module o_xor (
  input  a,
  input  b,
  output out_3
);

  wire o_and_1_out_3, o_and_2_out_3, o_not_1_out_2, o_not_2_out_2;

  o_not o_not_1 (.a(a), .out_2(o_not_1_out_2));
  o_not o_not_2 (.a(b), .out_2(o_not_2_out_2));
  o_and o_and_1 (.a(a), .b(o_not_2_out_2), .out_3(o_and_1_out_3));
  o_and o_and_2 (.a(o_not_1_out_2), .b(b), .out_3(o_and_2_out_3));
  o_or o_or_1 (.b(o_and_2_out_3), .a(o_and_1_out_3), .out_3(out_3));
endmodule

module mux (
  input  sel,
  input  a,
  input  b,
  output out_4
);

  wire o_and_1_out_3, o_and_2_out_3, o_not_1_out_2;

  o_not o_not_1 (.a(sel), .out_2(o_not_1_out_2));
  o_and o_and_1 (.a(sel), .b(b), .out_3(o_and_1_out_3));
  o_and o_and_2 (.a(o_not_1_out_2), .b(a), .out_3(o_and_2_out_3));
  o_or o_or_1 (.b(o_and_1_out_3), .a(o_and_2_out_3), .out_3(out_4));
endmodule

module dmux (
  input  sel,
  input  a,
  output out_3,
  output out_4
);

  wire o_not_1_out_2;

  o_not o_not_1 (.a(sel), .out_2(o_not_1_out_2));
  o_and o_and_1 (.a(o_not_1_out_2), .b(a), .out_3(out_3));
  o_and o_and_2 (.a(sel), .b(a), .out_3(out_4));
endmodule

module not4 (
  input  [3:0] a,
  output [3:0] out_2
);

  o_not o_not_1 (.a(a[0]), .out_2(out_2[0]));
  o_not o_not_2 (.a(a[1]), .out_2(out_2[1]));
  o_not o_not_3 (.a(a[2]), .out_2(out_2[2]));
  o_not o_not_4 (.a(a[3]), .out_2(out_2[3]));
endmodule

module and4 (
  input  [3:0] a,
  input  [3:0] b,
  output [3:0] out_3
);

  o_and o_and_1 (.a(a[0]), .b(b[0]), .out_3(out_3[0]));
  o_and o_and_2 (.a(a[1]), .b(b[1]), .out_3(out_3[1]));
  o_and o_and_3 (.a(a[2]), .b(b[2]), .out_3(out_3[2]));
  o_and o_and_4 (.a(a[3]), .b(b[3]), .out_3(out_3[3]));
endmodule

module mux4way4 (
  input  [1:0] in_1,
  input  [3:0] a,
  input  [3:0] b,
  input  [3:0] c,
  input  [3:0] d,
  output [3:0] out_6
);

  wire [3:0] mux4_1_out_4, mux4_2_out_4;

  mux4 mux4_1 (.in_1(a), .in_2(b), .in_3(in_1[1]), .out_4(mux4_1_out_4));
  mux4 mux4_2 (.in_1(c), .in_2(d), .in_3(in_1[1]), .out_4(mux4_2_out_4));
  mux4 mux4_3 (.in_1(mux4_1_out_4), .in_2(mux4_2_out_4), .in_3(in_1[0]), .out_4(out_6));
endmodule

module or4 (
  input  [3:0] a,
  input  [3:0] b,
  output [3:0] out_3
);

  o_or o_or_1 (.b(b[0]), .a(a[0]), .out_3(out_3[0]));
  o_or o_or_2 (.b(b[1]), .a(a[1]), .out_3(out_3[1]));
  o_or o_or_3 (.b(b[2]), .a(a[2]), .out_3(out_3[2]));
  o_or o_or_4 (.b(b[3]), .a(a[3]), .out_3(out_3[3]));
endmodule

module or8way (
  input  [7:0] in_1,
  output out_2
);

  wire o_or_1_out_3, o_or_2_out_3;
  wire [3:0] or4_1_out_3;

  or4 or4_1 (.a(in_1[3:0]), .b(in_1[7:4]), .out_3(or4_1_out_3));
  o_or o_or_1 (.b(or4_1_out_3[1]), .a(or4_1_out_3[0]), .out_3(o_or_1_out_3));
  o_or o_or_2 (.b(or4_1_out_3[3]), .a(or4_1_out_3[2]), .out_3(o_or_2_out_3));
  o_or o_or_3 (.b(o_or_2_out_3), .a(o_or_1_out_3), .out_3(out_2));
endmodule

module mux8way4 (
  input  [2:0] in_1,
  input  [3:0] in_2,
  input  [3:0] in_3,
  input  [3:0] in_4,
  input  [3:0] in_5,
  input  [3:0] in_6,
  input  [3:0] in_7,
  input  [3:0] in_8,
  input  [3:0] in_9,
  output [3:0] out_10
);

  wire [3:0] mux4way4_1_out_6, mux4way4_2_out_6;

  mux4way4 mux4way4_1 (.in_1(in_1[2:1]), .a(in_2), .b(in_3), .c(in_4), .d(in_5), .out_6(mux4way4_1_out_6));
  mux4way4 mux4way4_2 (.in_1(in_1[2:1]), .a(in_6), .b(in_7), .c(in_8), .d(in_9), .out_6(mux4way4_2_out_6));
  mux4 mux4_1 (.in_1(mux4way4_2_out_6), .in_2(mux4way4_1_out_6), .in_3(in_1[0]), .out_4(out_10));
endmodule

module mux4 (
  input  [3:0] in_1,
  input  [3:0] in_2,
  input  in_3,
  output [3:0] out_4
);

  wire [3:0] and4_1_out_3, and4_2_out_3, not4_1_out_2;

  not4 not4_1 (.a({4{in_3}}), .out_2(not4_1_out_2));
  and4 and4_1 (.a(in_1), .b(not4_1_out_2), .out_3(and4_1_out_3));
  and4 and4_2 (.a({4{in_3}}), .b(in_2), .out_3(and4_2_out_3));
  or4 or4_1 (.a(and4_1_out_3), .b(and4_2_out_3), .out_3(out_4));
endmodule

module dmux4 (
  input  in_1,
  input  [1:0] in_2,
  output out_3,
  output out_4,
  output out_5,
  output out_6
);

  wire dmux_1_out_3, dmux_1_out_4;

  dmux dmux_1 (.a(in_1), .sel(in_2[1]), .out_3(dmux_1_out_3), .out_4(dmux_1_out_4));
  dmux dmux_2 (.a(dmux_1_out_3), .sel(in_2[0]), .out_3(out_3), .out_4(out_4));
  dmux dmux_3 (.a(dmux_1_out_4), .sel(in_2[0]), .out_3(out_5), .out_4(out_6));
endmodule

module dmux8 (
  input  in_1,
  input  [2:0] in_2,
  output out_3,
  output out_4,
  output out_5,
  output out_6,
  output out_7,
  output out_8,
  output out_9,
  output out_10
);

  wire dmux_1_out_3, dmux_1_out_4;

  dmux dmux_1 (.a(in_1), .sel(in_2[2]), .out_3(dmux_1_out_3), .out_4(dmux_1_out_4));
  dmux4 dmux4_1 (.in_1(dmux_1_out_3), .in_2(in_2[1:0]), .out_3(out_3), .out_4(out_4), .out_5(out_5), .out_6(out_6));
  dmux4 dmux4_2 (.in_1(dmux_1_out_4), .in_2(in_2[1:0]), .out_3(out_7), .out_4(out_8), .out_5(out_9), .out_6(out_10));
endmodule
