// Logisim project 2lab.circ as structural Verilog: 14 circuits, main circuit main
module main (
  input  a,
  input  b,
  output sum,
  output carry
);

  and and_1 (carry, a, b);
  xor xor_1 (sum, a, b);
endmodule

module halfadder (
  input  a,
  input  b,
  output sum,
  output carry
);

  and and_1 (carry, a, b);
  xor xor_1 (sum, a, b);
endmodule

module fulladder (
  input  carryIn,
  input  a,
  input  b,
  output sum,
  output carry
);

  wire halfadder_1_carry, halfadder_2_carry, xor_1_out;

  xor xor_1 (xor_1_out, a, b);
  halfadder halfadder_1 (.a(a), .b(b), .carry(halfadder_1_carry));  // open: sum
  or or_1 (carry, halfadder_1_carry, halfadder_2_carry);
  halfadder halfadder_2 (.a(carryIn), .b(xor_1_out), .carry(halfadder_2_carry));  // open: sum
  xor xor_2 (sum, carryIn, xor_1_out);
endmodule

module adder4 (
  input  [3:0] b,
  input  [3:0] a,
  input  in_3,
  output carry,
  output [3:0] out_5
);

  wire fulladder_1_carry, fulladder_2_carry, fulladder_3_carry;

  fulladder fulladder_1 (.carryIn(b[0]), .a(a[0]), .b(in_3), .sum(out_5[0]), .carry(fulladder_1_carry));
  fulladder fulladder_2 (.carryIn(b[1]), .a(a[1]), .b(fulladder_1_carry), .sum(out_5[1]), .carry(fulladder_2_carry));
  fulladder fulladder_3 (.carryIn(b[2]), .a(a[2]), .b(fulladder_2_carry), .sum(out_5[2]), .carry(fulladder_3_carry));
  fulladder fulladder_4 (.carryIn(b[3]), .a(a[3]), .b(fulladder_3_carry), .sum(out_5[3]), .carry(carry));
endmodule

module incrementer4 (
  input  [3:0] a,
  output [3:0] out_2
);

  adder4 adder4_1 (.b(a), .a(4'b0000), .in_3(1'b1), .out_5(out_2));  // open: carry
endmodule

module negativeadder4 (
  input  [3:0] a,
  input  [3:0] b,
  output [3:0] out_3
);

  wire [3:0] not_1_out;

  assign not_1_out = ~b;  // NOT_Gate not_1, 4 bits wide
  adder4 adder4_1 (.b(a), .a(not_1_out), .in_3(1'b1), .out_5(out_3));  // open: carry
endmodule

module sumOrDiff4 (
  input  [3:0] b,
  input  k,
  input  [3:0] a,
  output overflow,
  output [3:0] res
);

  wire xnor_1_out, xor_1_out;
  wire [3:0] multiplexer_1_out, not_1_out;

  assign not_1_out = ~b;  // NOT_Gate not_1, 4 bits wide
  Multiplexer #(.width(4)) multiplexer_1 (.in0(b), .in1(not_1_out), .out(multiplexer_1_out), .sel(k));
  xnor xnor_1 (xnor_1_out, multiplexer_1_out[3], a[3]);
  adder4 adder4_1 (.b(multiplexer_1_out), .a(a), .in_3(k), .out_5(res));  // open: carry
  xor xor_1 (xor_1_out, a[3], res[3]);
  and and_1 (overflow, xnor_1_out, xor_1_out);
endmodule

module eqcomp4 (
  input  [3:0] in_1,
  input  [3:0] in_2,
  output out_3
);

  wire [3:0] xnor_1_out;

  assign xnor_1_out = ~(in_1 ^ in_2);  // XNOR_Gate xnor_1, 4 bits wide
  and and_1 (out_3, xnor_1_out[0], xnor_1_out[1], xnor_1_out[2], xnor_1_out[3]);
endmodule

module magcomp4 (
  input  [3:0] b,
  input  [3:0] a,
  output out_3
);

  wire xor_1_out;
  wire [3:0] sumordiff4_1_res;

  xor xor_1 (xor_1_out, b[3], a[3]);
  sumOrDiff4 sumordiff4_1 (.b(b), .k(1'b1), .a(a), .res(sumordiff4_1_res));  // open: overflow
  or or_1 (out_3, xor_1_out, sumordiff4_1_res[3]);
endmodule

module alu (
  input  [2:0] control,
  input  [31:0] b,
  input  [31:0] a,
  output [31:0] res,
  output negative,
  output zero,
  output overflow
);

  wire adder_1_cout;
  wire [31:0] adder_1_out, and_1_out, multiplexer_1_out, multiplexer_2_out, not_1_out, or_1_out;

  assign not_1_out = ~b;  // NOT_Gate not_1, 32 bits wide
  Multiplexer #(.width(32)) multiplexer_1 (.in0(b), .in1(not_1_out), .out(multiplexer_1_out), .sel(control[2]));
  assign and_1_out = multiplexer_1_out & a;  // AND_Gate and_1, 32 bits wide
  assign or_1_out = multiplexer_1_out | a;  // OR_Gate or_1, 32 bits wide
  Adder #(.width(32)) adder_1 (.a(a), .b(multiplexer_1_out), .out(adder_1_out), .cin(control[2]), .cout(adder_1_cout));
  Multiplexer #(.width(32)) multiplexer_2 (
    .in0(32'h1), .in1({32{1'b0}}), .out(multiplexer_2_out), .sel(adder_1_out[31]));
  Multiplexer #(.select(2), .width(32)) multiplexer_3 (
    .in0(and_1_out), .in1(or_1_out), .in2(adder_1_out), .in3(multiplexer_2_out), .out({negative, res[30:0]}),
    .sel(control[1:0]));
  or32 or32_1 (.in_1({negative, res[30:0]}), .out_2(zero));

  assign res[31] = negative;
endmodule

module or32 (
  input  [31:0] in_1,
  output out_2
);

  wire or_1_out;

  or or_1 (or_1_out, in_1[0], in_1[1], in_1[2], in_1[3], in_1[4], in_1[5], in_1[6], in_1[7], in_1[8], in_1[9], in_1[10], in_1[11], in_1[12], in_1[13], in_1[14], in_1[15], in_1[16], in_1[17], in_1[18], in_1[19], in_1[20], in_1[21], in_1[22], in_1[23], in_1[24], in_1[25], in_1[26], in_1[27], in_1[28], in_1[29], in_1[30], in_1[31]);
  not not_1 (out_2, or_1_out);
endmodule

module leftshift (
  input  [1:0] in_1,
  input  [3:0] in_2,
  output [3:0] out_3
);

  Multiplexer #(.select(2)) multiplexer_1 (
    .in0(in_2[3]), .in1(in_2[2]), .in2(in_2[1]), .in3(in_2[0]), .out(out_3[3]), .sel(in_1));
  Multiplexer #(.select(2)) multiplexer_2 (
    .in0(in_2[2]), .in1(in_2[1]), .in2(in_2[0]), .in3(1'b0), .out(out_3[2]), .sel(in_1));
  Multiplexer #(.select(2)) multiplexer_3 (
    .in0(in_2[1]), .in1(in_2[0]), .in2(1'b0), .in3(1'b0), .out(out_3[1]), .sel(in_1));
  Multiplexer #(.select(2)) multiplexer_4 (
    .in0(in_2[0]), .in1(1'b0), .in2(1'b0), .in3(1'b0), .out(out_3[0]), .sel(in_1));
endmodule

module logshiftleft (
  input  [1:0] in_1,
  input  [3:0] in_2,
  output [3:0] out_3
);

  Multiplexer #(.select(2)) multiplexer_1 (
    .in0(in_2[3]), .in1(1'b0), .in2(1'b0), .in3(1'b0), .out(out_3[3]), .sel(in_1));
  Multiplexer #(.select(2)) multiplexer_2 (
    .in0(in_2[2]), .in1(in_2[3]), .in2(1'b0), .in3(1'b0), .out(out_3[2]), .sel(in_1));
  Multiplexer #(.select(2)) multiplexer_3 (
    .in0(in_2[1]), .in1(in_2[2]), .in2(in_2[3]), .in3(1'b0), .out(out_3[1]), .sel(in_1));
  Multiplexer #(.select(2)) multiplexer_4 (
    .in0(in_2[0]), .in1(in_2[1]), .in2(in_2[2]), .in3(in_2[3]), .out(out_3[0]), .sel(in_1));
endmodule

module arshiftright (
  input  [1:0] in_1,
  input  [3:0] in_2,
  output [3:0] out_3
);

  Multiplexer #(.select(2)) multiplexer_1 (
    .in0(in_2[3]), .in1(in_2[3]), .in2(in_2[3]), .in3(in_2[3]), .out(out_3[3]), .sel(in_1));
  Multiplexer #(.select(2)) multiplexer_2 (
    .in0(in_2[2]), .in1(in_2[3]), .in2(in_2[3]), .in3(in_2[3]), .out(out_3[2]), .sel(in_1));
  Multiplexer #(.select(2)) multiplexer_3 (
    .in0(in_2[1]), .in1(in_2[2]), .in2(in_2[3]), .in3(in_2[3]), .out(out_3[1]), .sel(in_1));
  Multiplexer #(.select(2)) multiplexer_4 (
    .in0(in_2[0]), .in1(in_2[1]), .in2(in_2[2]), .in3(in_2[3]), .out(out_3[0]), .sel(in_1));
endmodule
