// Logisim project 3lab.circ as structural Verilog
module srLatch (
  input  R,
  input  S,
  output Q,
  output notQ
);

  nor nor_1 (Q, R, notQ);
  nor nor_2 (notQ, Q, S);
endmodule

module dLatch (
  input  CLK,
  input  D,
  output Q,
  output notQ
);

  wire and_1_out, and_2_out, not_1_out;

  not not_1 (not_1_out, D);
  and and_1 (and_1_out, CLK, not_1_out);
  and and_2 (and_2_out, CLK, D);
  srLatch srlatch_1 (.R(and_1_out), .S(and_2_out), .Q(Q), .notQ(notQ));
endmodule

module dflipflops (
  input  CLK,
  input  D,
  output Q
);

  wire dlatch_1_q, not_1_out;

  not not_1 (not_1_out, CLK);
  dLatch dlatch_1 (.CLK(not_1_out), .D(D), .Q(dlatch_1_q));  // open: notQ
  dLatch dlatch_2 (.CLK(CLK), .D(dlatch_1_q), .Q(Q));  // open: notQ
endmodule

module enabledFlipFlop (
  input  CLK,
  input  D,
  input  EN,
  output Q
);

  wire and_1_out;

  and and_1 (and_1_out, CLK, EN);
  dflipflops dflipflops_1 (.CLK(and_1_out), .D(D), .Q(Q));
endmodule

module resetFlipFlop (
  input  CLK,
  input  d,
  input  reset,
  output out_4
);

  wire and_1_out, not_1_out;

  not not_1 (not_1_out, reset);
  and and_1 (and_1_out, d, not_1_out);
  dflipflops dflipflops_1 (.CLK(CLK), .D(and_1_out), .Q(out_4));
endmodule

module asyncResetDLatch (
  input  CLK,
  input  D,
  input  reset,
  output Q,
  output notQ
);

  wire and_1_out, not_1_out, or_1_out;

  not not_1 (not_1_out, reset);
  and and_1 (and_1_out, D, not_1_out);
  or or_1 (or_1_out, CLK, reset);
  dLatch dlatch_1 (.CLK(or_1_out), .D(and_1_out), .Q(Q), .notQ(notQ));
endmodule

module asyncResetDFlipFlop (
  input  CLK,
  input  D,
  input  reset,
  output Q
);

  wire asyncresetdlatch_1_q, not_1_out;

  not not_1 (not_1_out, CLK);
  asyncResetDLatch asyncresetdlatch_1 (.CLK(not_1_out), .D(D), .reset(reset), .Q(asyncresetdlatch_1_q));  // open: notQ
  asyncResetDLatch asyncresetdlatch_2 (.CLK(CLK), .D(asyncresetdlatch_1_q), .reset(reset), .Q(Q));  // open: notQ
endmodule

module asyncDFlipFlop (
  input  CLK,
  input  D,
  output Q
);

  wire asyncdlatch_1_q, not_1_out, or_1_out;

  or or_1 (or_1_out, not_1_out, D);
  not not_1 (not_1_out, CLK);
  asyncDLatch asyncdlatch_1 (.CLK(or_1_out), .D(D), .Q(asyncdlatch_1_q));  // open: notQ
  asyncDLatch asyncdlatch_2 (.CLK(CLK), .D(asyncdlatch_1_q), .Q(Q));  // open: notQ
endmodule

module syncRSLatch (
  input  R,
  input  CLK,
  input  S,
  output Q,
  output notQ
);

  wire and_1_out, and_2_out;

  and and_1 (and_1_out, R, CLK);
  and and_2 (and_2_out, CLK, S);
  nor nor_1 (Q, and_1_out, notQ);
  nor nor_2 (notQ, Q, and_2_out);
endmodule

module syncDLatch (
  input  CLK,
  input  D,
  output Q,
  output notQ
);

  wire and_1_out, and_2_out, not_1_out;

  and and_1 (and_1_out, CLK, not_1_out);
  not not_1 (not_1_out, D);
  and and_2 (and_2_out, CLK, D);
  syncRSLatch syncrslatch_1 (.R(and_1_out), .CLK(CLK), .S(and_2_out), .Q(Q), .notQ(notQ));
endmodule

module logiDtrigger (
  input  CLK,
  input  EN,
  input  AsyncSet,
  input  asyncReset,
  input  D,
  output Q
);

  wire and_1_out, dlatch_1_q, not_1_out, or_1_out, or_2_out, or_3_out;

  or or_1 (or_1_out, not_1_out, AsyncSet);
  or or_2 (or_2_out, AsyncSet, D);
  and and_1 (and_1_out, or_1_out, EN);
  not not_1 (not_1_out, CLK);
  or or_3 (or_3_out, CLK, AsyncSet);
  dLatch dlatch_1 (.CLK(and_1_out), .D(or_2_out), .Q(dlatch_1_q));  // open: notQ
  asyncResetDLatch asyncresetdlatch_1 (.CLK(or_3_out), .D(dlatch_1_q), .reset(asyncReset), .Q(Q));  // open: notQ
endmodule

module asyncDLatch (
  input  CLK,
  input  D,
  output Q,
  output notQ
);

  wire and_1_out, not_1_out;

  not not_1 (not_1_out, D);
  and and_1 (and_1_out, CLK, not_1_out);
  srLatch srlatch_1 (.R(and_1_out), .S(D), .Q(Q), .notQ(notQ));
endmodule

module bit4Register (
  input  CLK,
  input  [3:0] D,
  output [3:0] out_3
);

  dflipflops dflipflops_1 (.CLK(CLK), .D(D[0]), .Q(out_3[0]));
  dflipflops dflipflops_2 (.CLK(CLK), .D(D[1]), .Q(out_3[1]));
  dflipflops dflipflops_3 (.CLK(CLK), .D(D[2]), .Q(out_3[2]));
  dflipflops dflipflops_4 (.CLK(CLK), .D(D[3]), .Q(out_3[3]));
endmodule

module registers (
  input  C,
  input  [7:0] A,
  input  [7:0] B,
  input  CLK
);

  wire [7:0] adder_1_out, register_1_q, register_2_q, xor_1_out;

  assign xor_1_out = A ^ B;  // XOR_Gate xor_1, 8 bits wide
  Adder adder_1 (.a(xor_1_out), .b(register_2_q), .out(adder_1_out), .cin(C));  // open: cout
  Register register_1 (.D(adder_1_out), .clk(CLK), .Q(register_1_q));  // open: en, clr
  Register register_2 (.D(register_1_q), .clk(CLK), .Q(register_2_q));  // open: en, clr
endmodule

module syncScheme (
  input  [7:0] in_1,
  output [7:0] out_2
);

  wire button_1_out, clock_1_out;
  wire [7:0] multiplexer_1_out, not_1_out, register_1_q;

  Clock clock_1 (.out(clock_1_out));
  assign not_1_out = ~in_1;  // NOT_Gate not_1, 8 bits wide
  Button button_1 (.out(button_1_out));
  Register register_1 (.D(out_2), .clk(clock_1_out), .Q(register_1_q));  // open: en, clr
  Multiplexer #(.width(8)) multiplexer_1 (.in0(in_1), .in1(not_1_out), .out(multiplexer_1_out), .sel(button_1_out));
  Adder adder_1 (.a(register_1_q), .b(multiplexer_1_out), .out(out_2));  // open: cin, cout
endmodule

module shiftRegisters (
  input  in_1,
  input  in_2,
  input  in_3,
  input  in_4,
  input  in_5,
  output out_6
);

  wire and_1_out, and_2_out, and_3_out, and_4_out, and_5_out, and_6_out, and_7_out, clock_1_out, not_1_out,
       or_1_out, or_2_out, or_3_out, register_1_q, register_2_q, register_3_q;

  not not_1 (not_1_out, in_5);
  Register #(.width(1)) register_1 (.D(and_1_out), .clk(clock_1_out), .Q(register_1_q));  // open: en, clr
  and and_1 (and_1_out, in_1, not_1_out);
  Clock clock_1 (.out(clock_1_out));
  and and_2 (and_2_out, in_2, not_1_out);
  and and_3 (and_3_out, in_5, register_1_q);
  or or_1 (or_1_out, and_2_out, and_3_out);
  Register #(.width(1)) register_2 (.D(or_1_out), .clk(clock_1_out), .Q(register_2_q));  // open: en, clr
  and and_4 (and_4_out, in_3, not_1_out);
  and and_5 (and_5_out, in_5, register_2_q);
  or or_2 (or_2_out, and_4_out, and_5_out);
  Register #(.width(1)) register_3 (.D(or_2_out), .clk(clock_1_out), .Q(register_3_q));  // open: en, clr
  and and_6 (and_6_out, in_4, not_1_out);
  and and_7 (and_7_out, in_5, register_3_q);
  or or_3 (or_3_out, and_6_out, and_7_out);
  Register #(.width(1)) register_4 (.D(or_3_out), .clk(clock_1_out), .Q(out_6));  // open: en, clr
endmodule

module ram8 (
  input  [7:0] inp,
  input  load,
  input  [2:0] k,
  input  CLK,
  output [7:0] outp
);

  wire demultiplexer_1_out0, demultiplexer_1_out1, demultiplexer_1_out2, demultiplexer_1_out3,
       demultiplexer_1_out4, demultiplexer_1_out5, demultiplexer_1_out6, demultiplexer_1_out7;
  wire [7:0] demultiplexer_2_out0, demultiplexer_2_out1, demultiplexer_2_out2, demultiplexer_2_out3,
       demultiplexer_2_out4, demultiplexer_2_out5, demultiplexer_2_out6, demultiplexer_2_out7, register_1_q,
       register_2_q, register_3_q, register_4_q, register_5_q, register_6_q, register_7_q, register_8_q;

  Demultiplexer #(.select(3)) demultiplexer_1 (
    .out0(demultiplexer_1_out0), .out1(demultiplexer_1_out1), .out2(demultiplexer_1_out2),
    .out3(demultiplexer_1_out3), .out4(demultiplexer_1_out4), .out5(demultiplexer_1_out5),
    .out6(demultiplexer_1_out6), .out7(demultiplexer_1_out7), .in(load), .sel(k));
  Demultiplexer #(.select(3), .width(8)) demultiplexer_2 (
    .out0(demultiplexer_2_out0), .out1(demultiplexer_2_out1), .out2(demultiplexer_2_out2),
    .out3(demultiplexer_2_out3), .out4(demultiplexer_2_out4), .out5(demultiplexer_2_out5),
    .out6(demultiplexer_2_out6), .out7(demultiplexer_2_out7), .in(inp), .sel(k));
  Register register_1 (.D(demultiplexer_2_out0), .en(demultiplexer_1_out0), .clk(CLK), .Q(register_1_q));  // open: clr
  Register register_2 (.D(demultiplexer_2_out1), .en(demultiplexer_1_out1), .clk(CLK), .Q(register_2_q));  // open: clr
  Register register_3 (.D(demultiplexer_2_out2), .en(demultiplexer_1_out2), .clk(CLK), .Q(register_3_q));  // open: clr
  Register register_4 (.D(demultiplexer_2_out3), .en(demultiplexer_1_out3), .clk(CLK), .Q(register_4_q));  // open: clr
  Register register_5 (.D(demultiplexer_2_out4), .en(demultiplexer_1_out4), .clk(CLK), .Q(register_5_q));  // open: clr
  Register register_6 (.D(demultiplexer_2_out5), .en(demultiplexer_1_out5), .clk(CLK), .Q(register_6_q));  // open: clr
  Register register_7 (.D(demultiplexer_2_out6), .en(demultiplexer_1_out6), .clk(CLK), .Q(register_7_q));  // open: clr
  Register register_8 (.D(demultiplexer_2_out7), .en(demultiplexer_1_out7), .clk(CLK), .Q(register_8_q));  // open: clr
  Multiplexer #(.select(3), .width(8)) multiplexer_1 (
    .in0(register_1_q), .in1(register_2_q), .in2(register_3_q), .in3(register_4_q), .in4(register_5_q),
    .in5(register_6_q), .in6(register_7_q), .in7(register_8_q), .out(outp));  // open: sel
endmodule

module ram64 (
  input  [7:0] inp,
  input  load,
  input  [5:0] k,
  output [7:0] outp
);

  wire clock_1_out, demultiplexer_1_out0, demultiplexer_1_out1, demultiplexer_1_out2, demultiplexer_1_out3,
       demultiplexer_1_out4, demultiplexer_1_out5, demultiplexer_1_out6, demultiplexer_1_out7;
  wire [7:0] ram8_1_outp, ram8_2_outp, ram8_3_outp, ram8_4_outp, ram8_5_outp, ram8_6_outp, ram8_7_outp,
       ram8_8_outp;

  Demultiplexer #(.select(3)) demultiplexer_1 (
    .out0(demultiplexer_1_out0), .out1(demultiplexer_1_out1), .out2(demultiplexer_1_out2),
    .out3(demultiplexer_1_out3), .out4(demultiplexer_1_out4), .out5(demultiplexer_1_out5),
    .out6(demultiplexer_1_out6), .out7(demultiplexer_1_out7), .in(load), .sel(k[5:3]));
  Clock clock_1 (.out(clock_1_out));
  ram8 ram8_1 (.inp(inp), .load(demultiplexer_1_out0), .k(k[2:0]), .CLK(clock_1_out), .outp(ram8_1_outp));
  ram8 ram8_2 (.inp(inp), .load(demultiplexer_1_out1), .k(k[2:0]), .CLK(clock_1_out), .outp(ram8_2_outp));
  ram8 ram8_3 (.inp(inp), .load(demultiplexer_1_out2), .k(k[2:0]), .CLK(clock_1_out), .outp(ram8_3_outp));
  ram8 ram8_4 (.inp(inp), .load(demultiplexer_1_out3), .k(k[2:0]), .CLK(clock_1_out), .outp(ram8_4_outp));
  ram8 ram8_5 (.inp(inp), .load(demultiplexer_1_out4), .k(k[2:0]), .CLK(clock_1_out), .outp(ram8_5_outp));
  ram8 ram8_6 (.inp(inp), .load(demultiplexer_1_out5), .k(k[2:0]), .CLK(clock_1_out), .outp(ram8_6_outp));
  ram8 ram8_7 (.inp(inp), .load(demultiplexer_1_out6), .k(k[2:0]), .CLK(clock_1_out), .outp(ram8_7_outp));
  ram8 ram8_8 (.inp(inp), .load(demultiplexer_1_out7), .k(k[2:0]), .CLK(clock_1_out), .outp(ram8_8_outp));
  Multiplexer #(.select(3), .width(8)) multiplexer_1 (
    .in0(ram8_1_outp), .in1(ram8_2_outp), .in2(ram8_3_outp), .in3(ram8_4_outp), .in4(ram8_5_outp),
    .in5(ram8_6_outp), .in6(ram8_7_outp), .in7(ram8_8_outp), .out(outp), .sel(k[5:3]));
endmodule

module PC (
  input  [15:0] inp,
  input  load,
  input  reset,
  input  inc,
  output [15:0] out_5
);

  wire clock_1_out;
  wire [15:0] multiplexer_1_out, multiplexer_2_out, register_1_q;

  Multiplexer #(.width(16)) multiplexer_1 (.in0({16{1'b0}}), .in1(16'h1), .out(multiplexer_1_out), .sel(inc));
  Register #(.width(16)) register_1 (
    .D(multiplexer_2_out), .clk(clock_1_out), .Q(register_1_q), .clr(reset));  // open: en
  Multiplexer #(.width(16)) multiplexer_2 (.in0(out_5), .in1(inp), .out(multiplexer_2_out), .sel(load));
  Clock clock_1 (.out(clock_1_out));
  Adder #(.width(16)) adder_1 (.a(register_1_q), .b(multiplexer_1_out), .out(out_5));  // open: cin, cout
endmodule
