// Logisim project alu_control.circ as structural Verilog: 1 circuit, main circuit main
module main (
  input  ALUOp1,
  input  ALUOp0,
  input  F5,
  input  F4,
  input  F3,
  input  F2,
  input  F1,
  input  F0,
  output Op3,
  output Op2,
  output Op1,
  output Op0
);

  wire and_1_out, and_2_out, and_3_out, and_4_out, and_5_out, not_1_out, not_2_out, not_3_out;

  not not_1 (not_1_out, ALUOp1);
  not not_2 (not_2_out, ALUOp0);
  not not_3 (not_3_out, F2);
  and and_1 (and_1_out, not_1_out, ALUOp0);
  and and_2 (and_2_out, ALUOp1, not_2_out, F1);
  and and_3 (and_3_out, not_2_out, not_3_out);
  and and_4 (and_4_out, ALUOp1, not_2_out, F0);
  and and_5 (and_5_out, ALUOp1, not_2_out, F3);
  or or_1 (Op2, and_1_out, and_2_out);
  or or_2 (Op1, not_1_out, and_3_out);
  or or_3 (Op0, and_4_out, and_5_out);

  assign Op3 = 1'b0;
endmodule
