// Logisim project 5task.circ as structural Verilog: 11 circuits, main circuit main
module main (
  input  in_1,
  input  in_2,
  input  in_3,
  input  in_4,
  input  in_5,
  input  in_6,
  input  in_7,
  input  in_8,
  input  [3:0] in_9,
  input  in_10,
  output [19:0] out_11
);

  wire and_1_out, Clock, mips_alu_1_p8, not_1_out, registerfile_1_p7;
  wire [4:0] decode_1_out_2, decode_1_out_3, decode_1_out_4, multiplexer_1_out;
  wire [15:0] decode_1_out_6;
  wire [25:0] decode_1_out_7;
  wire [31:0] adder_1_out, adder_2_out, bit_extender_1_out, mips_alu_1_p6, mips_alu_1_p7, mips_ram_1_p6,
       mipsprogramrom_1_p2, multiplexer_2_out, multiplexer_3_out, multiplexer_4_out, register_1_q,
       registerfile_1_p1, registerfile_1_p8, shifter_1_out;

  Register #(.width(32)) register_1 (.D(multiplexer_3_out), .Q(register_1_q), .clk(Clock), .clr(in_1));  // open: en
  Adder #(.width(32)) adder_1 (.a(32'h4), .b(register_1_q), .out(adder_1_out));  // open: cin, cout
  Clock clock_1 (.out(Clock));
  // MIPSProgramROM mipsprogramrom_1: pin names not known; wires that end beside it: register_1_q, mipsprogramrom_1_p2
  Decode decode_1 (
    .in_1(mipsprogramrom_1_p2), .out_2(decode_1_out_2), .out_3(decode_1_out_3), .out_4(decode_1_out_4),
    .out_6(decode_1_out_6), .out_7(decode_1_out_7));  // open: out_5, out_8, out_9
  // Probe on mipsprogramrom_1_p2
  // Probe on mipsprogramrom_1_p2
  not not_1 (not_1_out, Clock);
  Multiplexer #(.width(5), .enable("false")) multiplexer_1 (
    .in0(decode_1_out_3), .in1(decode_1_out_4), .out(multiplexer_1_out), .sel(in_3));
  assign bit_extender_1_out = {{16{decode_1_out_6[15]}}, decode_1_out_6};  // Bit_Extender bit_extender_1
  // RegisterFile registerfile_1: pin names not known; wires that end beside it: registerfile_1_p1, not_1_out, in_2, multiplexer_1_out, decode_1_out_2, decode_1_out_3, registerfile_1_p7, registerfile_1_p8
  Multiplexer #(.width(32), .enable("false")) multiplexer_2 (
    .in0(registerfile_1_p8), .in1(bit_extender_1_out), .out(multiplexer_2_out), .sel(in_6));
  Shifter #(.width(32)) shifter_1 (.in(bit_extender_1_out), .\dist (5'b00010), .out(shifter_1_out));
  Adder #(.width(32)) adder_2 (.a(adder_1_out), .b(shifter_1_out), .out(adder_2_out));  // open: cin, cout
  // Mips_ALU mips_alu_1: pin names not known; wires that end beside it: registerfile_1_p7, multiplexer_2_out, in_9, decode_1_out_7, adder_1_out, mips_alu_1_p6, mips_alu_1_p7, mips_alu_1_p8, mips_alu_1_p6, out_11
  and and_1 (and_1_out, in_8, mips_alu_1_p8);
  Multiplexer #(.width(32), .enable("false")) multiplexer_3 (
    .in0(multiplexer_4_out), .in1(mips_alu_1_p7), .out(multiplexer_3_out), .sel(in_10));
  Multiplexer #(.width(32), .enable("false")) multiplexer_4 (
    .in0(adder_1_out), .in1(adder_2_out), .out(multiplexer_4_out), .sel(and_1_out));
  // MIPS_RAM mips_ram_1: pin names not known; wires that end beside it: out_11, registerfile_1_p8, in_5, Clock, in_4, mips_ram_1_p6
  Multiplexer #(.width(32), .enable("false")) multiplexer_5 (
    .in0(mips_alu_1_p6), .in1(mips_ram_1_p6), .out(registerfile_1_p1), .sel(in_7));

  // Other names for the same wires on the sheet: ALU_Operation[3:0] = in_9; ALUSrc = in_6; Branch = in_8;
  //   Jump = in_10; MemRead = in_4; MemToReg = in_7; MemWrite = in_5; RegDst = in_3; RegWrite = in_2; Reset = in_1

  // Notes on the sheet:
  //   0010 - add
  //   1100 - nor
endmodule

module PC (
  input  CLK,
  input  reset,
  output [31:0] Q
);

  wire [31:0] adder_1_out;

  Adder #(.width(32)) adder_1 (.a(Q), .b(32'h4), .out(adder_1_out));  // open: cin, cout
  Register #(.width(32)) register_1 (.D(adder_1_out), .Q(Q), .clk(CLK), .clr(reset));  // open: en
endmodule

module testPC (
  input  in_1
);

  wire clock_1_out;
  wire [31:0] pc_1_q;

  Clock clock_1 (.out(clock_1_out));
  PC pc_1 (.CLK(clock_1_out), .reset(in_1), .Q(pc_1_q));
  // MIPSProgramROM mipsprogramrom_1: pin names not known; wires that end beside it: pc_1_q
endmodule

module Decode (
  input  [31:0] in_1,
  output [4:0] out_2,
  output [4:0] out_3,
  output [4:0] out_4,
  output [4:0] out_5,
  output [15:0] out_6,
  output [25:0] out_7,
  output [5:0] out_8,
  output [5:0] out_9
);


  assign out_2 = in_1[25:21];
  assign out_3 = in_1[20:16];
  assign out_4 = in_1[15:11];
  assign out_5 = in_1[10:6];
  assign out_6 = in_1[15:0];
  assign out_7 = in_1[25:0];
  assign out_8 = in_1[31:26];
  assign out_9 = in_1[5:0];

  // Other names for the same wires on the sheet: addr[25:0] = in_1[25:0]; rt[4:0] = in_1[20:16];
  //   rs[4:0] = in_1[25:21]; funct[5:0] = in_1[5:0]; imm[15:0] = in_1[15:0]; shamt[4:0] = in_1[10:6];
  //   rd[4:0] = in_1[15:11]; opcode[5:0] = in_1[31:26]
endmodule

module ControlBase (
  input  op5,
  input  op4,
  input  op3,
  input  op2,
  input  op1,
  input  op0,
  output RegWrite,
  output RegDst,
  output ALUSrc,
  output MemToReg,
  output MemWrite,
  output MemRead,
  output Branch,
  output Jump,
  output ALU1,
  output ALU0
);

  wire and_2_out, and_3_out, not_1_out, not_2_out, not_3_out, not_5_out, not_6_out, not_7_out, not_8_out;

  not not_1 (not_1_out, op2);
  not not_2 (not_2_out, op1);
  not not_3 (not_3_out, op3);
  not not_4 (RegDst, op0);
  and and_1 (MemWrite, op5, op3);
  not not_5 (not_5_out, op3);
  not not_6 (not_6_out, op0);
  not not_7 (not_7_out, op2);
  not not_8 (not_8_out, op0);
  and and_2 (and_2_out, not_1_out, not_2_out);
  and and_3 (and_3_out, op5, not_3_out);
  and and_4 (MemRead, op5, not_5_out);
  and and_5 (Jump, op1, not_6_out);
  and and_6 (ALU1, not_7_out, not_8_out);
  or or_1 (RegWrite, and_2_out, and_3_out);

  assign ALU0 = op2;
  assign ALUSrc = op0;
  assign Branch = op2;
  assign MemToReg = op1;
endmodule

module ALUControlBase (
  input  ALUOp1,
  input  ALUOp0,
  input  F5,
  input  F4,
  input  F3,
  input  F2,
  input  F1,
  input  F0,
  output Op3,
  output Op2,
  output Op1,
  output Op0
);

  wire not_1_out, not_2_out, not_3_out, not_4_out, not_5_out, or_1_out, or_2_out, or_3_out, or_5_out,
       or_6_out, or_7_out, or_8_out;

  not not_1 (not_1_out, ALUOp1);
  not not_2 (not_2_out, ALUOp0);
  not not_3 (not_3_out, F3);
  not not_4 (not_4_out, F2);
  not not_5 (not_5_out, F1);
  or or_1 (or_1_out, ALUOp1, ALUOp0);
  or or_2 (or_2_out, not_1_out, F3, F1, F0);
  or or_3 (or_3_out, not_1_out, F3, not_4_out, F1);
  or or_4 (Op1, not_1_out, F3, not_4_out, F1);
  or or_5 (or_5_out, not_2_out, not_3_out);
  or or_6 (or_6_out, F3, F0);
  or or_7 (or_7_out, F3, F2);
  or or_8 (or_8_out, F3, not_5_out);
  and and_1 (Op2, or_1_out, or_2_out, or_3_out);
  and and_2 (Op0, ALUOp1, or_5_out, or_6_out, or_7_out, or_8_out);

  assign Op3 = 1'b0;
endmodule

module ALUControl (
  input  [1:0] ALUOp,
  input  [5:0] funct,
  output [3:0] ALUOperation
);

  ALUControlBase alucontrolbase_1 (
    .ALUOp1(ALUOp[1]), .ALUOp0(ALUOp[0]), .F5(funct[5]), .F4(funct[4]), .F3(funct[3]), .F2(funct[2]),
    .F1(funct[1]), .F0(funct[0]), .Op3(ALUOperation[3]), .Op2(ALUOperation[2]), .Op1(ALUOperation[1]),
    .Op0(ALUOperation[0]));
endmodule

module Control (
  input  [5:0] opcode,
  input  [5:0] funct,
  output RegWrite,
  output RegDst,
  output ALUSrc,
  output MemToReg,
  output MemWrite,
  output MemRead,
  output Branch,
  output Jump,
  output [3:0] ALUOperation,
  output ExOp,
  output slt_u,
  output SLTOp
);

  wire comparator_1_eq;
  wire [1:0] controlbase_1_alu0;
  wire [3:0] alucontrol_1_aluoperation, shifter_1_out;

  Comparator #(.width(4), .mode("unsigned")) comparator_1 (
    .a(opcode[5:2]), .b(4'b0011), .eq(comparator_1_eq));  // open: gt, lt
  Comparator #(.width(5), .mode("unsigned")) comparator_2 (.a(opcode[5:1]), .b(5'b00101), .eq(SLTOp));  // open: gt, lt
  ControlBase controlbase_1 (
    .op5(opcode[0]), .op4(opcode[1]), .op3(opcode[2]), .op2(opcode[3]), .op1(opcode[4]), .op0(opcode[5]),
    .RegWrite(RegWrite), .RegDst(RegDst), .ALUSrc(ALUSrc), .MemToReg(MemToReg), .MemWrite(MemWrite),
    .MemRead(MemRead), .Branch(Branch), .Jump(Jump), .ALU1(controlbase_1_alu0[1]),
    .ALU0(controlbase_1_alu0[0]));
  Shifter #(.width(4)) shifter_1 (.in(opcode[3:0]), .\dist (2'b01), .out(shifter_1_out));
  ALUControl alucontrol_1 (.ALUOp(controlbase_1_alu0), .funct(funct), .ALUOperation(alucontrol_1_aluoperation));
  Multiplexer #(.width(4)) multiplexer_1 (
    .in0(alucontrol_1_aluoperation), .in1(shifter_1_out), .out(ALUOperation), .sel(comparator_1_eq));  // open: en
  not not_1 (ExOp, comparator_1_eq);

  assign slt_u = opcode[0];
endmodule

module task1_addiu (
  input  in_1
);

  wire ALUSrc, Branch, CLK, ExOp, Jump, MemRead, MemToReg, MemWrite, RegDst, RegWrite, slt_u, SLTOp;
  wire [3:0] ALU_Operation;
  wire [4:0] decode_1_out_2, decode_1_out_3;
  wire [5:0] funct, opcode;
  wire [15:0] decode_1_out_6;
  wire [31:0] extender_1_out, mips_alu_1_p4, mipsprogramrom_1_p2, pc_1_q, registerfile_1_p1,
       registerfile_1_p7, slt_1_out_4;

  PC pc_1 (.CLK(CLK), .reset(in_1), .Q(pc_1_q));
  Clock clock_1 (.out(CLK));
  // MIPSProgramROM mipsprogramrom_1: pin names not known; wires that end beside it: pc_1_q, mipsprogramrom_1_p2
  Decode decode_1 (
    .in_1(mipsprogramrom_1_p2), .out_2(decode_1_out_2), .out_3(decode_1_out_3), .out_6(decode_1_out_6),
    .out_8(opcode), .out_9(funct));  // open: out_4, out_5, out_7
  // Probe on opcode
  // Probe on funct
  Extender extender_1 (.imm(decode_1_out_6), .ExOp(ExOp), .Out(extender_1_out));
  Control control_1 (
    .opcode(opcode), .funct(funct), .RegWrite(RegWrite), .RegDst(RegDst), .ALUSrc(ALUSrc),
    .MemToReg(MemToReg), .MemWrite(MemWrite), .MemRead(MemRead), .Branch(Branch), .Jump(Jump),
    .ALUOperation(ALU_Operation), .ExOp(ExOp), .SLTOp(SLTOp), .slt_u(slt_u));
  // RegisterFile registerfile_1: pin names not known; wires that end beside it: registerfile_1_p1, CLK, RegWrite, decode_1_out_3, decode_1_out_2, decode_1_out_3, registerfile_1_p7
  // Probe on ALU_Operation
  // Mips_ALU mips_alu_1: pin names not known; wires that end beside it: registerfile_1_p7, extender_1_out, ALU_Operation, mips_alu_1_p4
  Multiplexer #(.width(32)) multiplexer_1 (
    .in0(mips_alu_1_p4), .in1(slt_1_out_4), .out(registerfile_1_p1), .sel(SLTOp));  // open: en
  slt slt_1 (.A(registerfile_1_p7), .B(decode_1_out_6), .slt_u(slt_u), .out_4(slt_1_out_4));
endmodule

module Extender (
  input  [15:0] imm,
  input  ExOp,
  output [31:0] Out
);

  wire [31:0] bit_extender_1_out, bit_extender_2_out;

  assign bit_extender_1_out = {{16{1'b0}}, imm};  // Bit_Extender bit_extender_1
  assign bit_extender_2_out = {{16{imm[15]}}, imm};  // Bit_Extender bit_extender_2
  Multiplexer #(.width(32)) multiplexer_1 (
    .in0(bit_extender_1_out), .in1(bit_extender_2_out), .out(Out), .sel(ExOp));  // open: en
endmodule

module slt (
  input  [31:0] A,
  input  [15:0] B,
  input  slt_u,
  output [31:0] out_4
);

  wire comparator_1_lt;
  wire [31:0] extender_1_out;

  Extender extender_1 (.imm(B), .ExOp(slt_u), .Out(extender_1_out));
  Comparator #(.width(32), .mode("unsigned")) comparator_1 (
    .a(A), .b(extender_1_out), .lt(comparator_1_lt));  // open: gt, eq
  assign out_4 = {{31{1'b0}}, comparator_1_lt};  // Bit_Extender bit_extender_1
endmodule
