// Logisim project rgr3.circ as structural Verilog: 8 circuits, main circuit InstructionDecode
module InstructionDecode (
  input  [31:0] Instruction,
  output [5:0] op,
  output [4:0] rs,
  output [4:0] rt,
  output [4:0] rd,
  output [4:0] shamt,
  output [5:0] funct,
  output [15:0] immediate,
  output [25:0] address
);


  assign address = Instruction[25:0];
  assign funct = Instruction[5:0];
  assign immediate = Instruction[15:0];
  assign op = Instruction[31:26];
  assign rd = Instruction[15:11];
  assign rs = Instruction[25:21];
  assign rt = Instruction[20:16];
  assign shamt = Instruction[10:6];

  // Notes on the sheet:
  //   J-type
  //   I-type
  //   R-type
endmodule

module ALU (
  input  [31:0] A,
  input  [31:0] B,
  input  [3:0] Operation,
  output Zero,
  output [31:0] Result,
  output Overflow
);

  wire getsign_1_sign, getsign_2_sign, getsign_3_sign, xor_1_out;
  wire [31:0] adder_1_out, and_1_out, getsign_1_out_2, getsign_2_out_2, getsign_3_out_2, multiplexer_1_out,
       multiplexer_2_out, not_1_out, not_2_out, or_1_out, setlsb_1_out_3;

  assign not_1_out = ~A;  // NOT_Gate not_1, 32 bits wide
  assign not_2_out = ~B;  // NOT_Gate not_2, 32 bits wide
  Multiplexer #(.width(32), .enable("false")) multiplexer_1 (
    .in0(A), .in1(not_1_out), .out(multiplexer_1_out), .sel(Operation[3]));
  Multiplexer #(.width(32), .enable("false")) multiplexer_2 (
    .in0(B), .in1(not_2_out), .out(multiplexer_2_out), .sel(Operation[2]));
  GetSign getsign_1 (.in_1(multiplexer_1_out), .out_2(getsign_1_out_2), .Sign(getsign_1_sign));
  GetSign getsign_2 (.in_1(multiplexer_2_out), .out_2(getsign_2_out_2), .Sign(getsign_2_sign));
  Overflow overflow_1 (
    .A(getsign_1_sign), .B(getsign_2_sign), .Overflow(Overflow), .Result(getsign_3_sign),
    .Operation(Operation[1:0]));
  assign and_1_out = getsign_1_out_2 & getsign_2_out_2;  // AND_Gate and_1, 32 bits wide
  assign or_1_out = getsign_1_out_2 | getsign_2_out_2;  // OR_Gate or_1, 32 bits wide
  GetSign getsign_3 (.in_1(adder_1_out), .out_2(getsign_3_out_2), .Sign(getsign_3_sign));
  Adder #(.width(32)) adder_1 (
    .a(getsign_1_out_2), .b(getsign_2_out_2), .out(adder_1_out), .cin(Operation[2]));  // open: cout
  xor xor_1 (xor_1_out, getsign_3_sign, Overflow);
  SetLSB setlsb_1 (.in_2({32{1'b0}}), .out_3(setlsb_1_out_3), .LSB(xor_1_out));
  Multiplexer #(.select(2), .width(32), .enable("false")) multiplexer_3 (
    .in0(and_1_out), .in1(or_1_out), .in2(getsign_3_out_2), .in3(setlsb_1_out_3), .out(Result),
    .sel(Operation[1:0]));
  Zero zero_1 (.in_1(Result), .out_2(Zero));
endmodule

module Overflow (
  input  Result,
  input  A,
  input  B,
  input  [1:0] Operation,
  output Overflow
);

  wire and_1_out, and_2_out, not_1_out, not_2_out, not_3_out, not_4_out, or_1_out;

  not not_1 (not_1_out, Result);
  not not_2 (not_2_out, A);
  not not_3 (not_3_out, B);
  not not_4 (not_4_out, Operation[0]);
  and and_1 (and_1_out, not_1_out, A, B);
  and and_2 (and_2_out, Result, not_2_out, not_3_out);
  or or_1 (or_1_out, and_1_out, and_2_out);
  and and_3 (Overflow, or_1_out, Operation[1], not_4_out);
endmodule

module SetLSB (
  input  LSB,
  input  [31:0] in_2,
  output [31:0] out_3
);


  assign out_3 = {in_2[31:1], LSB};
endmodule

module GetSign (
  input  [31:0] in_1,
  output [31:0] out_2,
  output Sign
);


  assign out_2 = in_1;
  assign Sign = in_1[31];
endmodule

module Zero (
  input  [31:0] in_1,
  output out_2
);

  wire or_1_out, or_2_out, or_3_out, or_4_out;

  or or_1 (or_1_out, in_1[0], in_1[1], in_1[2], in_1[3], in_1[4], in_1[5], in_1[6]);
  or or_2 (or_2_out, in_1[7], in_1[8], in_1[9], in_1[10], in_1[11], in_1[12], in_1[13], in_1[14], in_1[15]);
  or or_3 (or_3_out, in_1[16], in_1[17], in_1[18], in_1[19], in_1[20], in_1[21], in_1[22], in_1[23], in_1[24]);
  or or_4 (or_4_out, in_1[25], in_1[26], in_1[27], in_1[28], in_1[29], in_1[30], in_1[31]);
  nor nor_1 (out_2, or_1_out, or_2_out, or_3_out, or_4_out);
endmodule

module FormAdress (
  input  [31:0] _32BitAddress,
  output [19:0] _20BitAddress
);


  assign _20BitAddress = _32BitAddress[19:0];
endmodule

module JumpAddr (
  input  [31:0] PC_4,
  input  [25:0] instr_index,
  output [31:0] branch_target_address
);


  assign branch_target_address = {PC_4[31:28], instr_index, 2'b00};
endmodule
