// Logisim project rgr3_logisim.circ as structural Verilog: 1 circuit, main circuit main
module main (
  input  in_1,
  input  in_2,
  input  in_3,
  input  in_4,
  input  in_5,
  input  in_6,
  input  in_7,
  input  in_8,
  input  [3:0] in_9,
  input  in_10,
  output [19:0] out_11
);

  wire alu_1_zero, and_1_out, Clock, not_1_out;
  wire [4:0] instructiondecode_1_rd, instructiondecode_1_rs, instructiondecode_1_rt, multiplexer_1_out;
  wire [15:0] instructiondecode_1_immediate;
  wire [25:0] instructiondecode_1_address;
  wire [31:0] adder_1_out, adder_2_out, alu_1_result, bit_extender_1_out, jumpaddr_1_branch_target_address,
       mips_ram_1_p6, mipsprogramrom_1_p2, multiplexer_2_out, multiplexer_3_out, multiplexer_4_out,
       register_1_q, registerfile_1_p1, registerfile_1_p7, registerfile_1_p8, shifter_1_out;

  Register #(.width(32)) register_1 (.D(multiplexer_3_out), .Q(register_1_q), .clk(Clock), .clr(in_1));  // open: en
  Adder #(.width(32)) adder_1 (.a(32'h4), .b(register_1_q), .out(adder_1_out));  // open: cin, cout
  Clock clock_1 (.out(Clock));
  // MIPSProgramROM mipsprogramrom_1: pin names not known; wires that end beside it: register_1_q, mipsprogramrom_1_p2
  InstructionDecode instructiondecode_1 (
    .Instruction(mipsprogramrom_1_p2), .rs(instructiondecode_1_rs), .rt(instructiondecode_1_rt),
    .rd(instructiondecode_1_rd), .immediate(instructiondecode_1_immediate),
    .address(instructiondecode_1_address));  // open: op, shamt, funct
  // Probe on mipsprogramrom_1_p2
  // Probe on mipsprogramrom_1_p2
  not not_1 (not_1_out, Clock);
  Multiplexer #(.width(5), .enable("false")) multiplexer_1 (
    .in0(instructiondecode_1_rt), .in1(instructiondecode_1_rd), .out(multiplexer_1_out), .sel(in_3));
  assign bit_extender_1_out = {{16{instructiondecode_1_immediate[15]}}, instructiondecode_1_immediate};  // Bit_Extender bit_extender_1
  // RegisterFile registerfile_1: pin names not known; wires that end beside it: registerfile_1_p1, not_1_out, in_2, multiplexer_1_out, instructiondecode_1_rs, instructiondecode_1_rt, registerfile_1_p7, registerfile_1_p8
  Multiplexer #(.width(32), .enable("false")) multiplexer_2 (
    .in0(registerfile_1_p8), .in1(bit_extender_1_out), .out(multiplexer_2_out), .sel(in_6));
  Shifter #(.width(32)) shifter_1 (.in(bit_extender_1_out), .\dist (5'b00010), .out(shifter_1_out));
  Adder #(.width(32)) adder_2 (.a(adder_1_out), .b(shifter_1_out), .out(adder_2_out));  // open: cin, cout
  JumpAddr jumpaddr_1 (
    .PC_4(adder_1_out), .instr_index(instructiondecode_1_address),
    .branch_target_address(jumpaddr_1_branch_target_address));
  ALU alu_1 (
    .A(registerfile_1_p7), .B(multiplexer_2_out), .Zero(alu_1_zero), .Result(alu_1_result), .Operation(in_9));  // open: Overflow
  FormAdress formadress_1 (._32BitAddress(alu_1_result), ._20BitAddress(out_11));
  and and_1 (and_1_out, in_8, alu_1_zero);
  Multiplexer #(.width(32), .enable("false")) multiplexer_3 (
    .in0(multiplexer_4_out), .in1(jumpaddr_1_branch_target_address), .out(multiplexer_3_out), .sel(in_10));
  Multiplexer #(.width(32), .enable("false")) multiplexer_4 (
    .in0(adder_1_out), .in1(adder_2_out), .out(multiplexer_4_out), .sel(and_1_out));
  // MIPS_RAM mips_ram_1: pin names not known; wires that end beside it: out_11, registerfile_1_p8, in_5, Clock, in_4, mips_ram_1_p6
  Multiplexer #(.width(32), .enable("false")) multiplexer_5 (
    .in0(alu_1_result), .in1(mips_ram_1_p6), .out(registerfile_1_p1), .sel(in_7));

  // Other names for the same wires on the sheet: ALU_Operation[3:0] = in_9; ALUSrc = in_6; Branch = in_8;
  //   Jump = in_10; MemRead = in_4; MemToReg = in_7; MemWrite = in_5; RegDst = in_3; RegWrite = in_2; Reset = in_1

  // Notes on the sheet:
  //   0010 - add
  //   1100 - nor
endmodule
