// Logisim project wwwwwww.circ as structural Verilog: 1 circuit, main circuit main
module main (
  input  Reset,
  input  in_2,
  input  [3:0] in_3
);

  wire Clock;
  wire [4:0] instructiondecode_1_rd, instructiondecode_1_rs, instructiondecode_1_rt;
  wire [31:0] adder_1_out, mipsprogramrom_1_p2, register_1_q, registerfile_1_p1, registerfile_1_p7,
       registerfile_1_p8;

  Clock u_Clock (.out(Clock));
  Register #(.width(32)) register_1 (.D(adder_1_out), .Q(register_1_q), .clk(Clock), .clr(Reset));  // open: en
  Adder #(.width(32)) adder_1 (.a(32'h4), .b(register_1_q), .out(adder_1_out));  // open: cin, cout
  // MIPSProgramROM mipsprogramrom_1: pin names not known; wires that end beside it: register_1_q, mipsprogramrom_1_p2
  // Probe on mipsprogramrom_1_p2
  InstructionDecode instructiondecode_1 (
    .Instruction(mipsprogramrom_1_p2), .rs(instructiondecode_1_rs), .rt(instructiondecode_1_rt),
    .rd(instructiondecode_1_rd));  // open: op, shamt, funct, immediate, address
  // RegisterFile registerfile_1: pin names not known; wires that end beside it: registerfile_1_p1, Clock, in_2, instructiondecode_1_rd, instructiondecode_1_rs, instructiondecode_1_rt, registerfile_1_p7, registerfile_1_p8
  ALU alu_1 (
    .A(registerfile_1_p7), .B(registerfile_1_p8), .Result(registerfile_1_p1), .Operation(in_3));  // open: Zero, Overflow

  // Other names for the same wires on the sheet: ALU_Operation[3:0] = in_3; RegWrite = in_2
endmodule
