// Logisim project rgr2.circ as structural Verilog
module moore_duo (
  input  inn,
  input  CLK,
  input  s2,
  input  s1,
  input  s0,
  output s2a,
  output s1a,
  output out_8,
  output s0a
);

  wire and_2_out, and_3_out, and_4_out, and_5_out, d_ff_1_q, d_ff_2_q, d_ff_3_q, not_1_out, not_2_out,
       not_3_out, not_4_out, not_5_out;

  not not_1 (not_1_out, d_ff_2_q);
  not not_2 (not_2_out, d_ff_3_q);
  not not_3 (not_3_out, inn);
  and and_1 (s2a, d_ff_2_q, d_ff_3_q, inn);
  and and_2 (and_2_out, not_1_out, d_ff_3_q, not_3_out);
  and and_3 (and_3_out, d_ff_2_q, not_2_out, not_3_out);
  and and_4 (and_4_out, not_1_out, inn);
  and and_5 (and_5_out, d_ff_2_q, not_2_out);
  or or_1 (s1a, and_2_out, and_3_out);
  or or_2 (s0a, and_4_out, and_5_out);
  D_Flip_Flop d_ff_1 (.D(s2a), .clk(CLK), .Q(d_ff_1_q));  // open: Qn, preset, reset
  D_Flip_Flop d_ff_2 (.D(s1a), .clk(CLK), .Q(d_ff_2_q));  // open: Qn, preset, reset
  D_Flip_Flop d_ff_3 (.D(s0a), .clk(CLK), .Q(d_ff_3_q));  // open: Qn, preset, reset
  not not_4 (not_4_out, d_ff_2_q);
  not not_5 (not_5_out, d_ff_3_q);
  and and_6 (out_8, d_ff_1_q, not_4_out, not_5_out);
endmodule

module meele_duo (
  input  inp,
  output S11,
  output S00,
  output outp
);

  wire and_1_out, and_2_out, and_3_out, clock_1_out, d_ff_1_q, d_ff_2_q, not_1_out, not_2_out, not_3_out;

  not not_1 (not_1_out, d_ff_1_q);
  not not_2 (not_2_out, d_ff_2_q);
  not not_3 (not_3_out, inp);
  and and_1 (and_1_out, not_1_out, d_ff_2_q, not_3_out);
  and and_2 (and_2_out, d_ff_1_q, not_2_out, not_3_out);
  and and_3 (and_3_out, d_ff_1_q, not_2_out);
  and and_4 (outp, d_ff_1_q, d_ff_2_q, inp);
  or or_1 (S11, and_1_out, and_2_out);
  or or_2 (S00, inp, and_3_out);
  D_Flip_Flop d_ff_1 (.D(S11), .clk(clock_1_out), .Q(d_ff_1_q));  // open: Qn, preset, reset
  D_Flip_Flop d_ff_2 (.D(S00), .clk(clock_1_out), .Q(d_ff_2_q));  // open: Qn, preset, reset
  Clock clock_1 (.out(clock_1_out));
endmodule

module meele_str (
  input  inp,
  output S33,
  output S22,
  output S11,
  output S00,
  output outp
);

  wire clock_1_out, d_ff_1_q, d_ff_2_q, d_ff_3_q, not_1_out, not_2_out, not_3_out;

  not not_1 (not_1_out, d_ff_2_q);
  not not_2 (not_2_out, d_ff_3_q);
  not not_3 (not_3_out, inp);
  and and_1 (S33, d_ff_2_q, not_3_out);
  and and_2 (S22, d_ff_3_q, not_3_out);
  and and_3 (S00, not_1_out, not_2_out, not_3_out);
  and and_4 (outp, d_ff_1_q, inp);
  Clock clock_1 (.out(clock_1_out));
  D_Flip_Flop d_ff_1 (.D(S33), .clk(clock_1_out), .Q(d_ff_1_q));  // open: Qn, preset, reset
  D_Flip_Flop d_ff_2 (.D(S22), .clk(clock_1_out), .Q(d_ff_2_q));  // open: Qn, preset, reset
  D_Flip_Flop d_ff_3 (.D(inp), .clk(clock_1_out), .Q(d_ff_3_q));  // open: Qn, preset, reset
  D_Flip_Flop d_ff_4 (.D(S00), .clk(clock_1_out));  // open: Q, Qn, preset, reset

  assign S11 = inp;
endmodule

module moore_str (
  input  inp,
  input  in_2,
  output S44,
  output S33,
  output S22,
  output S11,
  output S00,
  output outp
);

  wire clock_1_out, d_ff_2_q, d_ff_3_q, d_ff_4_q, d_ff_5_q, not_1_out, not_2_out, not_3_out, not_4_out,
       not_5_out, not_6_out;

  not not_1 (not_1_out, outp);
  not not_2 (not_2_out, d_ff_2_q);
  not not_3 (not_3_out, d_ff_3_q);
  not not_4 (not_4_out, d_ff_4_q);
  not not_5 (not_5_out, d_ff_5_q);
  not not_6 (not_6_out, inp);
  and and_1 (S44, not_1_out, not_4_out, not_5_out, inp);
  and and_2 (S33, d_ff_3_q, not_6_out);
  and and_3 (S22, d_ff_4_q, not_6_out);
  and and_4 (S11, not_2_out, not_3_out, inp);
  and and_5 (S00, not_3_out, not_4_out, not_6_out);
  Clock clock_1 (.out(clock_1_out));
  D_Flip_Flop d_ff_1 (.D(S44), .clk(clock_1_out), .Q(outp), .reset(in_2));  // open: Qn, preset
  D_Flip_Flop d_ff_2 (.D(S33), .clk(clock_1_out), .Q(d_ff_2_q), .reset(in_2));  // open: Qn, preset
  D_Flip_Flop d_ff_3 (.D(S22), .clk(clock_1_out), .Q(d_ff_3_q), .reset(in_2));  // open: Qn, preset
  D_Flip_Flop d_ff_4 (.D(S11), .clk(clock_1_out), .Q(d_ff_4_q), .reset(in_2));  // open: Qn, preset
  D_Flip_Flop d_ff_5 (.D(S00), .clk(clock_1_out), .Q(d_ff_5_q), .reset(in_2));  // open: Qn, preset
endmodule
